// Logisim project Advanced Digital Clock.circ as structural Verilog: 7 circuits, main circuit main
module main (
  input  [3:0] minutes_1s,
  input  [3:0] minutes_10s,
  input  [3:0] hour_10s,
  input  [3:0] hour_1s,
  input  in_5,
  input  in_6,
  output out_7,
  output out_8,
  output out_9,
  output out_10
);

  wire and_1_out, and_2_out, clock_1_out, d_ff_7_q, d_ff_15_q, d_ff_15_qn, hours_12_1s_1_o0,
       hours_12_1s_1_o1, hours_12_1s_1_o2, hours_12_1s_1_o3, hours_12_10s_1_o0, hours_12_10s_2_o0,
       hours_24_1s_1_o0, hours_24_1s_1_o1, hours_24_1s_1_o2, hours_24_1s_1_o3, hours_24_10s_1_o1,
       hours_24_10s_1_o2, minutes_1s_1_o0, minutes_1s_1_o1, minutes_1s_1_o2, minutes_1s_1_o3,
       minutes_10s_1_o0, minutes_10s_1_o1, minutes_10s_1_o2, nor_1_out, nor_2_out, nor_3_out, nor_4_out,
       nor_5_out, nor_6_out, not_1_out, not_2_out, not_3_out, not_4_out, not_5_out, not_6_out, or_1_out,
       or_2_out;
  wire [1:0] d_ff_1_q;
  wire [2:0] d_ff_14_q;
  wire [3:0] bit_extender_1_out, bit_extender_2_out, d_ff_6_q, d_ff_11_q, d_ff_19_q, multiplexer_1_out,
       multiplexer_2_out;

  or or_1 (or_1_out, nor_2_out, nor_1_out);
  hours_24_10s hours_24_10s_1 (.a(d_ff_1_q[1]), .b(d_ff_1_q[0]), .o1(hours_24_10s_1_o1), .o2(hours_24_10s_1_o2));
  nor nor_1 (nor_1_out, not_1_out, d_ff_1_q[0], d_ff_6_q[3], d_ff_6_q[2], d_ff_6_q[1], d_ff_6_q[0]);
  nor nor_2 (nor_2_out, d_ff_6_q[3], d_ff_6_q[2], d_ff_6_q[1], d_ff_6_q[0]);
  D_Flip_Flop d_ff_1 (.clk(or_1_out), .D(hours_24_10s_1_o2), .Q(d_ff_1_q[0]));  // open: Qn, preset, en, reset
  D_Flip_Flop d_ff_2 (.clk(or_1_out), .D(hours_24_10s_1_o1), .Q(d_ff_1_q[1]));  // open: Qn, preset, en, reset
  not not_1 (not_1_out, d_ff_1_q[1]);
  assign bit_extender_1_out = {{2{1'b0}}, d_ff_1_q};  // Bit_Extender bit_extender_1
  hours_24_1s hours_24_1s_1 (
    .carry_in(d_ff_1_q[1]), .carry_in2(d_ff_1_q[0]), .a(d_ff_6_q[3]), .b(d_ff_6_q[2]), .c(d_ff_6_q[1]),
    .d(d_ff_6_q[0]), .o3(hours_24_1s_1_o3), .o2(hours_24_1s_1_o2), .o1(hours_24_1s_1_o1),
    .o0(hours_24_1s_1_o0));
  D_Flip_Flop d_ff_3 (.clk(nor_4_out), .D(hours_24_1s_1_o3), .Q(d_ff_6_q[3]));  // open: Qn, preset, en, reset
  D_Flip_Flop d_ff_4 (.clk(nor_4_out), .D(hours_24_1s_1_o2), .Q(d_ff_6_q[2]));  // open: Qn, preset, en, reset
  D_Flip_Flop d_ff_5 (.clk(nor_4_out), .D(hours_24_1s_1_o1), .Q(d_ff_6_q[1]));  // open: Qn, preset, en, reset
  D_Flip_Flop d_ff_6 (.clk(nor_4_out), .D(hours_24_1s_1_o0), .Q(d_ff_6_q[0]));  // open: Qn, preset, en, reset
  assign bit_extender_2_out = {{3{1'b0}}, d_ff_7_q};  // Bit_Extender bit_extender_2
  Multiplexer #(.width(4)) multiplexer_1 (
    .in0(bit_extender_2_out), .in1(bit_extender_1_out), .out(multiplexer_1_out), .sel(in_6));  // open: en
  D_Flip_Flop d_ff_7 (.clk(or_2_out), .D(hours_12_10s_1_o0), .Q(d_ff_7_q));  // open: Qn, preset, en, reset
  hours_12_10s hours_12_10s_1 (.a(d_ff_7_q), .o0(hours_12_10s_1_o0));
  or or_2 (or_2_out, nor_3_out, and_1_out);
  and and_1 (and_1_out, d_ff_7_q, not_2_out, not_3_out, not_4_out, d_ff_11_q[0]);
  Comparator #(.width(4)) comparator_1 (.a(d_ff_19_q), .b(minutes_1s), .eq(out_7));  // open: gt, lt
  Comparator #(.width(4)) comparator_2 (.a({in_5, d_ff_14_q}), .b(minutes_10s), .eq(out_8));  // open: gt, lt
  Comparator #(.width(4)) comparator_3 (.a(multiplexer_1_out), .b(hour_10s), .eq(out_9));  // open: gt, lt
  Comparator #(.width(4)) comparator_4 (.a(multiplexer_2_out), .b(hour_1s), .eq(out_10));  // open: gt, lt
  Hex_Digit_Display hex_digit_display_1 (.value(multiplexer_1_out));  // open: dp
  Hex_Digit_Display hex_digit_display_2 (.value(multiplexer_2_out));  // open: dp
  Multiplexer #(.width(4)) multiplexer_2 (
    .in0(d_ff_11_q), .in1(d_ff_6_q), .out(multiplexer_2_out), .sel(in_6));  // open: en
  not not_2 (not_2_out, d_ff_11_q[3]);
  not not_3 (not_3_out, d_ff_11_q[2]);
  not not_4 (not_4_out, d_ff_11_q[1]);
  nor nor_3 (nor_3_out, d_ff_11_q[3], d_ff_11_q[2], d_ff_11_q[1], d_ff_11_q[0]);
  LED led_1 (.in(1'b1));
  LED led_2 (.in(1'b1));
  Hex_Digit_Display hex_digit_display_3 (.value({in_5, d_ff_14_q}));  // open: dp
  Hex_Digit_Display hex_digit_display_4 (.value(d_ff_19_q));  // open: dp
  hours_12_1s hours_12_1s_1 (
    .Carry_in(d_ff_7_q), .a(d_ff_11_q[3]), .b(d_ff_11_q[2]), .c(d_ff_11_q[1]), .d(d_ff_11_q[0]),
    .o3(hours_12_1s_1_o3), .o2(hours_12_1s_1_o2), .o1(hours_12_1s_1_o1), .o0(hours_12_1s_1_o0));
  LED led_3 (.in(and_2_out));
  and and_2 (and_2_out, out_9, out_10, out_8, out_7);
  LED led_4 (.in(d_ff_15_q));
  LED led_5 (.in(d_ff_15_qn));
  D_Flip_Flop d_ff_8 (.clk(nor_4_out), .D(hours_12_1s_1_o3), .Q(d_ff_11_q[3]));  // open: Qn, preset, en, reset
  D_Flip_Flop d_ff_9 (.clk(nor_4_out), .D(hours_12_1s_1_o2), .Q(d_ff_11_q[2]));  // open: Qn, preset, en, reset
  D_Flip_Flop d_ff_10 (.clk(nor_4_out), .D(hours_12_1s_1_o1), .Q(d_ff_11_q[1]));  // open: Qn, preset, en, reset
  D_Flip_Flop d_ff_11 (.clk(nor_4_out), .D(hours_12_1s_1_o0), .Q(d_ff_11_q[0]));  // open: Qn, preset, en, reset
  nor nor_4 (nor_4_out, d_ff_14_q[2], d_ff_14_q[1], d_ff_14_q[0]);
  not not_5 (not_5_out, d_ff_7_q);
  not not_6 (not_6_out, d_ff_11_q[1]);
  nor nor_5 (nor_5_out, not_5_out, d_ff_11_q[3], d_ff_11_q[2], not_6_out, d_ff_11_q[0]);
  minutes_10s minutes_10s_1 (
    .a(d_ff_14_q[2]), .b(d_ff_14_q[1]), .c(d_ff_14_q[0]), .o2(minutes_10s_1_o2), .o1(minutes_10s_1_o1),
    .o0(minutes_10s_1_o0));
  hours_12_10s hours_12_10s_2 (.a(d_ff_15_q), .o0(hours_12_10s_2_o0));
  nor nor_6 (nor_6_out, d_ff_19_q[3], d_ff_19_q[2], d_ff_19_q[1], d_ff_19_q[0]);
  D_Flip_Flop d_ff_12 (.clk(nor_6_out), .D(minutes_10s_1_o2), .Q(d_ff_14_q[2]));  // open: Qn, preset, en, reset
  D_Flip_Flop d_ff_13 (.clk(nor_6_out), .D(minutes_10s_1_o1), .Q(d_ff_14_q[1]));  // open: Qn, preset, en, reset
  D_Flip_Flop d_ff_14 (.clk(nor_6_out), .D(minutes_10s_1_o0), .Q(d_ff_14_q[0]));  // open: Qn, preset, en, reset
  D_Flip_Flop d_ff_15 (
    .clk(nor_5_out), .D(hours_12_10s_2_o0), .Q(d_ff_15_q), .Qn(d_ff_15_qn));  // open: preset, en, reset
  minutes_1s minutes_1s_1 (
    .a(d_ff_19_q[3]), .b(d_ff_19_q[2]), .c(d_ff_19_q[1]), .d(d_ff_19_q[0]), .o3(minutes_1s_1_o3),
    .o2(minutes_1s_1_o2), .o1(minutes_1s_1_o1), .o0(minutes_1s_1_o0));
  Clock clock_1 (.out(clock_1_out));
  D_Flip_Flop d_ff_16 (.clk(clock_1_out), .D(minutes_1s_1_o3), .Q(d_ff_19_q[3]));  // open: Qn, preset, en, reset
  D_Flip_Flop d_ff_17 (.clk(clock_1_out), .D(minutes_1s_1_o2), .Q(d_ff_19_q[2]));  // open: Qn, preset, en, reset
  D_Flip_Flop d_ff_18 (.clk(clock_1_out), .D(minutes_1s_1_o1), .Q(d_ff_19_q[1]));  // open: Qn, preset, en, reset
  D_Flip_Flop d_ff_19 (.clk(clock_1_out), .D(minutes_1s_1_o0), .Q(d_ff_19_q[0]));  // open: Qn, preset, en, reset

  // Notes on the sheet:
  //   hours 24_10s
  //   hours 24_1s
  //   hours 10s
  //   hours 1s
  //   Alarm
  //   PM
  //   AM
  //   minutes 10s
  //   hours 10s
  //   minutes 1s
endmodule

module minutes_1s (
  input  a,
  input  b,
  input  c,
  input  d,
  output o3,
  output o2,
  output o1,
  output o0
);

  wire and_1_out, and_2_out, and_3_out, and_4_out, and_5_out, and_6_out, and_7_out, not_1_out, not_2_out,
       not_3_out, not_4_out, not_5_out, not_6_out, not_7_out;

  and and_1 (and_1_out, b, c, d);
  and and_2 (and_2_out, a, not_1_out);
  not not_1 (not_1_out, d);
  not not_2 (not_2_out, b);
  and and_3 (and_3_out, not_2_out, c, d);
  and and_4 (and_4_out, b, not_3_out);
  not not_3 (not_3_out, c);
  and and_5 (and_5_out, b, not_4_out);
  not not_4 (not_4_out, d);
  not not_5 (not_5_out, a);
  not not_6 (not_6_out, c);
  and and_6 (and_6_out, not_5_out, not_6_out, d);
  and and_7 (and_7_out, c, not_7_out);
  not not_7 (not_7_out, d);
  not not_8 (o0, d);
  or or_1 (o3, and_1_out, and_2_out);
  or or_2 (o2, and_3_out, and_4_out, and_5_out);
  or or_3 (o1, and_6_out, and_7_out);
endmodule

module minutes_10s (
  input  a,
  input  b,
  input  c,
  output o2,
  output o1,
  output o0
);

  wire and_1_out, and_2_out, and_3_out, and_4_out, not_1_out, not_2_out, not_3_out, not_4_out;

  not not_1 (not_1_out, c);
  not not_2 (not_2_out, a);
  not not_3 (not_3_out, b);
  not not_4 (not_4_out, c);
  not not_5 (o0, c);
  and and_1 (and_1_out, b, c);
  and and_2 (and_2_out, a, not_1_out);
  and and_3 (and_3_out, not_2_out, not_3_out, c);
  and and_4 (and_4_out, b, not_4_out);
  or or_1 (o2, and_1_out, and_2_out);
  or or_2 (o1, and_3_out, and_4_out);
endmodule

module hours_12_1s (
  input  Carry_in,
  input  a,
  input  b,
  input  c,
  input  d,
  output o3,
  output o2,
  output o1,
  output o0
);

  wire and_1_out, and_2_out, and_3_out, and_4_out, and_5_out, and_6_out, and_7_out, not_1_out, not_2_out,
       not_3_out, not_4_out, not_5_out, not_6_out, not_7_out, not_8_out;

  not not_1 (not_1_out, d);
  not not_2 (not_2_out, b);
  not not_3 (not_3_out, c);
  not not_4 (not_4_out, d);
  not not_5 (not_5_out, a);
  not not_6 (not_6_out, c);
  not not_7 (not_7_out, Carry_in);
  not not_8 (not_8_out, d);
  not not_9 (o0, d);
  and and_1 (and_1_out, b, c, d);
  and and_2 (and_2_out, a, not_1_out);
  and and_3 (and_3_out, not_2_out, c, d);
  and and_4 (and_4_out, b, not_3_out);
  and and_5 (and_5_out, b, not_4_out);
  and and_6 (and_6_out, not_5_out, not_6_out, d);
  and and_7 (and_7_out, not_7_out, c, not_8_out);
  or or_1 (o3, and_1_out, and_2_out);
  or or_2 (o2, and_3_out, and_4_out, and_5_out);
  or or_3 (o1, and_6_out, and_7_out);
endmodule

module hours_12_10s (
  input  a,
  output o0
);

  not not_1 (o0, a);
endmodule

module hours_24_10s (
  input  a,
  input  b,
  output o1,
  output o2
);

  wire not_1_out, not_2_out;

  not not_1 (not_1_out, a);
  not not_2 (not_2_out, b);
  and and_1 (o2, not_1_out, not_2_out);

  assign o1 = b;
endmodule

module hours_24_1s (
  input  carry_in,
  input  carry_in2,
  input  a,
  input  b,
  input  c,
  input  d,
  output o3,
  output o2,
  output o1,
  output o0
);

  wire and_1_out, and_2_out, and_3_out, and_4_out, and_5_out, and_6_out, and_7_out, and_8_out, and_9_out,
       and_10_out, not_1_out, not_2_out, not_3_out, not_4_out, not_5_out, not_6_out, not_7_out, not_8_out,
       not_9_out, not_10_out, not_11_out, not_12_out;

  not not_1 (not_1_out, d);
  not not_2 (not_2_out, carry_in);
  not not_3 (not_3_out, b);
  not not_4 (not_4_out, carry_in);
  not not_5 (not_5_out, c);
  not not_6 (not_6_out, carry_in);
  not not_7 (not_7_out, d);
  not not_8 (not_8_out, b);
  not not_9 (not_9_out, b);
  not not_10 (not_10_out, a);
  not not_11 (not_11_out, c);
  not not_12 (not_12_out, d);
  not not_13 (o0, d);
  and and_1 (and_1_out, b, c, d);
  and and_2 (and_2_out, a, not_1_out);
  and and_3 (and_3_out, not_2_out, not_3_out, c, d);
  and and_4 (and_4_out, not_4_out, b, not_5_out);
  and and_5 (and_5_out, not_6_out, b, not_7_out);
  and and_6 (and_6_out, a, not_8_out, c, d);
  and and_7 (and_7_out, carry_in2, not_9_out, c, d);
  and and_8 (and_8_out, not_10_out, not_11_out, d);
  and and_9 (and_9_out, c, not_12_out);
  and and_10 (and_10_out, carry_in, b);
  or or_1 (o3, and_1_out, and_2_out);
  or or_2 (o2, and_3_out, and_4_out, and_5_out, and_6_out, and_7_out);
  or or_3 (o1, and_8_out, and_9_out, and_10_out);
endmodule
